# Fritzing sketch pantalla-oled-ssd1306 (saved by Fritzing 0.9.3b)
breadboards: 2

parts:
  U1 = ESP32-38PinWide [part_number=ESP32-38PinWide]
  J1 = SSD1306 128x64 [form="♂ (male)" package=THT]

nets:
  N1: U1.3.3, J1.VCC
  GND: U1.GND, J1.GND
  N2: U1.GPIO21, J1.SDA
  N3: U1.GPIO22, J1.SCL

custom parts:
  ESP32-38PinWide: Generic 38-Pin ESP32 with wide format (only access to one side of pins on a breadboard) based on Stephen Lilley's HiLetgo ESP-WROOM-32 ESP32 ESP-32S Development Board.
  SSD1306 128x64: These displays are small, only about 1" diagonal, but very readable due to the high contrast of an OLED display. This display is made of 128x64 individual white OLED pixels, each one is turned on or off by the controller chip. Because the display makes its own light, no backlight is required. This reduces the power required to run the OLED and is why the display has such high contrast; we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
